# Fritzing sketch analogarray (saved by Fritzing 0.9.3b)
breadboards: 1

parts:
  Part1 = Arduino Uno (Rev3)
  R4 = Photocell (LDR) [package=THT]
  R3 = Rotary Potentiometer (Small) [maximum_resistance=100kΩ package=THT]
  LED2 = RGB LED (com. cathode, rgb) [package="5 mm [THT]"]
  POT1 = Breadboard Trimpot
  R8 = Temperature Sensor (Thermistor) [thermistor_type=NTC package=THT]
  Part3 = Thumb Joystick
  R7 = Resistor [tolerance=±5% resistance=220 package=THT]
  R6 = Resistor [tolerance=±5% resistance=220 package=THT]
  R2 = Resistor [tolerance=±5% resistance=220 package=THT]
  R5 = Resistor [tolerance=±5% resistance=10k package=THT]
  R10 = Resistor [tolerance=±5% resistance=10k package=THT]

nets:
  N1: Part1.A0, R4.pin_1, R5.Pin_0
  N2: Part1.A1, R3.wiper
  N3: Part1.A2, POT1.PIN2
  N4: Part1.A3, Part3.HORZ
  N5: Part1.A4/SDA, Part3.VERT
  N6: Part1.A5/SCL, R8.pin_1, R10.Pin_0
  N7: Part1.D9_PWM, R2.Pin_1
  N8: Part1.D10_PWM/SS, R6.Pin_1
  N9: Part1.D11_PWM/MOSI, R7.Pin_1
  N10: Part1.D2, Part3.SEL
  5V: Part1.5V, R4.pin_0, R3.leg1, POT1.PIN1, R8.pin_0, Part3.VCC
  GND: Part1.GND, R3.leg2, LED2.common_cathode, POT1.PIN3, Part3.GND, R5.Pin_1, R10.Pin_1
  N11: LED2.red_anode, R2.Pin_0
  N12: LED2.green_anode, R6.Pin_0
  N13: LED2.blue_anode, R7.Pin_0
