# Fritzing sketch resistor (saved by Fritzing 0.9.3b)
breadboards: 1

parts:
  Part1 = Arduino Uno (Rev3)
  LED2 = RGB LED (com. cathode, rgb) [package="5 mm [THT]"]
  R7 = Resistor [tolerance=±5% resistance=220 package=THT]
  R6 = Resistor [tolerance=±5% resistance=220 package=THT]
  R2 = Resistor [tolerance=±5% resistance=220 package=THT]
  R9 = Resistor [tolerance=±5% resistance=10k package=THT]
  R10 = Resistor [tolerance=±5% resistance=10k package=THT]

nets:
  N1: Part1.A2, Part1.5V, R9.Pin_0
  N2: Part1.A3, Part1.GND, LED2.common_cathode, R10.Pin_0
  N3: Part1.A4/SDA, R9.Pin_1
  N4: Part1.A5/SCL, R10.Pin_1
  N5: Part1.D9_PWM, R2.Pin_1
  N6: Part1.D10_PWM/SS, R6.Pin_1
  N7: Part1.D11_PWM/MOSI, R7.Pin_1
  N8: LED2.red_anode, R2.Pin_0
  N9: LED2.green_anode, R6.Pin_0
  N10: LED2.blue_anode, R7.Pin_0
