# Fritzing sketch motors (saved by Fritzing 0.9.3b)
breadboards: 1

parts:
  Part1 = Arduino Uno (Rev3)
  LED2 = RGB LED (com. cathode, rgb) [package="5 mm [THT]"]
  R7 = Resistor [tolerance=±5% resistance=220 package=THT]
  R6 = Resistor [tolerance=±5% resistance=220 package=THT]
  R2 = Resistor [tolerance=±5% resistance=220 package=THT]
  Q1 = NPN-Transistor [package="TO92 [THT]"]
  M1 = DC Motor
  J1 = Basic Servo
  POT1 = Breadboard Trimpot
  DHT1 = DHT11 Humitidy and Temperature Sensor
  D1 = Rectifier Diode [part_number=1N4001 package="300 mil [THT]"]
  R8 = Resistor [tolerance=±5% resistance=270 package=THT]
  J2 = Piezo Speaker

nets:
  N1: Part1.A0, POT1.PIN2
  N2: Part1.D9_PWM, R2.Pin_1
  N3: Part1.D10_PWM/SS, R6.Pin_1
  N4: Part1.D11_PWM/MOSI, R7.Pin_1
  N5: Part1.D2, DHT1.DATA
  N6: Part1.D3_PWM, R8.Pin_0
  N7: Part1.D5_PWM, J1.pulse
  N8: Part1.D6_PWM, J2.pin2
  5V: Part1.5V, M1.pin_2, J1.vcc, POT1.PIN1, DHT1.VDD, D1.cathode
  GND: Part1.GND, LED2.common_cathode, Q1.E, J1.gnd, POT1.PIN3, DHT1.GND, J2.pin1
  N9: LED2.red_anode, R2.Pin_0
  N10: LED2.green_anode, R6.Pin_0
  N11: LED2.blue_anode, R7.Pin_0
  N12: Q1.B, R8.Pin_1
  N13: Q1.C, M1.pin_1, D1.anode

notes:
  220 Ohm Resistors on RGB LED
  DHT11 breakout rearranges the internal pins as shown in the wire colors below.
  220 Ohm Resistor for Transistor

custom parts:
  DHT11 Humitidy and Temperature Sensor: DHT11 Humidity and Temperature Sensor
