# Fritzing sketch remotelight (saved by Fritzing 0.9.3b)
breadboards: 1

parts:
  Part1 = Arduino Uno (Rev3)
  LED2 = RGB LED (com. cathode, rgb) [package="5 mm [THT]"]
  R7 = Resistor [tolerance=±5% resistance=220 package=THT]
  R6 = Resistor [tolerance=±5% resistance=220 package=THT]
  R2 = Resistor [tolerance=±5% resistance=220 package=THT]
  DHT1 = DHT11 Humitidy and Temperature Sensor
  Part2 = Adafruit I2C+SPI LCD Backpack [part_number="Adafruit #292"]  # not connected
  U1 = LCD-16X2 [package=lcd-16x2_nosilk]  # not connected
  IR1 = TSOP312.., 314.. [package=THT]
  JP1 = Header 4 [package=1x04-smd]
  POT1 = Breadboard Trimpot

nets:
  N1: Part1.A4/SDA, JP1.3
  N2: Part1.A5/SCL, JP1.4
  N3: Part1.D9_PWM, R2.Pin_1
  N4: Part1.D10_PWM/SS, R6.Pin_1
  N5: Part1.D11_PWM/MOSI, R7.Pin_1
  N6: Part1.D2, DHT1.DATA
  N7: Part1.D6_PWM, IR1.Data
  N8: Part1.3V3, IR1.Vs
  5V: Part1.5V, DHT1.VDD, JP1.2, POT1.PIN1
  GND: Part1.GND, LED2.common_cathode, DHT1.GND, IR1.GND, JP1.1, POT1.PIN3
  N9: LED2.red_anode, R2.Pin_0
  N10: LED2.green_anode, R6.Pin_0
  N11: LED2.blue_anode, R7.Pin_0

notes:
  220 Ohm Resistors on RGB LED
  DHT11 breakout rearranges the internal pins as shown in the wire colors below.
  GND VCC SDA SCL

custom parts:
  DHT11 Humitidy and Temperature Sensor: DHT11 Humidity and Temperature Sensor
  Adafruit I2C+SPI LCD Backpack: LCD backpacks reduce the number of pins needed to connect to an LCD. LCDs are a fun and easy way to have your microcontroller project talk back to you. Character LCDs are common, and easy to get, available in tons of colors and sizes. We've written tutorials on using character LCDs with an Arduino (or similar microcontroller) but find that the number of pins necessary to control the LCD can be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
