# Fritzing sketch separated_power (saved by Fritzing 0.9.3b)
breadboards: 1

parts:
  NEOPIXEL2 = Neopixel Strip -- Black (30/m) [part_number=1376]
  Part1 = Arduino Uno (Rev3) - ICSP
  JACK1 = 2.1mm Barrel Jack with Terminal Block
  L1 = Solenoid
  Q2 = NPN-Transistor [package="TO92 [THT]"]
  D2 = Rectifier Diode [part_number=1N4001 package="300 mil [THT]"]
  R9 = Resistor [tolerance=±5% resistance=270 package=THT]
  R11 = Resistor [tolerance=±5% resistance=247 package=THT]
  C2 = Capacitor Polarized [package=cpol-radial-1000uf-25v]

nets:
  GND: NEOPIXEL2.GND, Part1.GND, JACK1.NEG, Q2.E, C2.-
  N1: NEOPIXEL2.Din, R11.Pin_0
  N2: NEOPIXEL2.+5V, JACK1.POS, L1.pin2, D2.cathode, C2.+
  N3: Part1.D6_PWM, R11.Pin_1
  N4: Part1.D7, R9.Pin_0
  N5: L1.pin1, Q2.C, D2.anode
  N6: Q2.B, R9.Pin_1

notes:
  220 Ohm Resistor for Transistor
  470 Ohm Resistor for LED Strip
  1000 uF Capacitor (optional)
  Power Supply, High Voltage or High Amperage

custom parts:
  Neopixel Strip -- Black (30/m): These NeoPixel strips have 30 digitally-addressable pixel LEDs per meter and are very affordable and are only 12.5 mm wide, 10 mm if you remove the strip from the casing.
